# Fritzing sketch kommunikator_v1 (saved by Fritzing 1.0.5)
circuit board: 7.05569cm x 10.0437cm
breadboards: 1

parts:
  MCU1 = Raspberry Pi Zero
  Adafruit_MAX1 = Adafruit MAX17048 LiPoly / LiIon Fuel Gauge and Battery Monitor [part_number=#5580]
  BAT1 = Battery Holders [package=battcom_20mm_pth]
  Bauteil1 = DS3231 [chip_label=DS3231 package=SO16]
  R1 = Resistor [tolerance=±5% resistance=4.3k power=0.25W package="1206 [SMD]"]
  R2 = Resistor [tolerance=±5% resistance=4.3k power=0.25W package="1206 [SMD]"]
  Mod2 = ossoyoo-lora-module
  S1 = Pushbutton [package="[THT]"]
  LED1 = RGB LED (com. cathode, rbg) [color="Red (633nm)" current=0.030A package="5 mm [THT]"]
  Sensor_Stecker1 = Generic female header - 6 pins [form="♀ (female)" package=THT]
  R3 = Resistor [tolerance=±5% power=0.25W resistance=4.7k package=THT]
  R4 = Resistor [tolerance=±5% power=0.25W resistance=150 package=THT]
  R5 = Resistor [tolerance=±5% power=0.25W resistance=150 package=THT]
  Bauteil2 = Barometric Pressure Sensor - BMP180 Breakout (GY-68)
  Q1 = Basic FET P-Channel [package="TO220 [THT]"]
  R6 = Resistor [tolerance=±5% power=0.25W resistance=100k package=THT]
  J3 = Generic female header - 2 pins [form="♀ (female)" package=THT]
  Q2 = NPN-Transistor [package="TO92 [THT]"]
  R8 = Resistor [tolerance=±5% power=0.25W resistance=220 package=THT]
  R9 = Resistor [tolerance=±5% power=0.25W resistance=220 package=THT]
  S2 = Pushbutton [package="[THT]"]
  D1 = Rectifier Diode [part_number=1N4148 package="300 mil [THT]"]
  J4 = female pin header, 3 pins [form="♀ (female)"]
  R10 = Resistor [tolerance=±5% power=0.25W resistance=330 package=THT]
  J5 = female pin header, 3 pins [form="♀ (female)"]

nets:
  VCC: MCU1.pin_1, MCU1.pin_17, Adafruit_MAX1.VCC, Bauteil1.VCC, R1.Pin_0, R2.Pin_1, Mod2.VCC, LED1.common_cathode, Sensor_Stecker1.3.3V, R3.Pin_1, Bauteil2.VCC
  N1: MCU1.pin_2, MCU1.pin_4, Q1.drain
  N2: MCU1.pin_3, Adafruit_MAX1.SDA, Bauteil1.SDA, R1.Pin_1, Sensor_Stecker1.SDA, Bauteil2.SDA
  N3: MCU1.pin_5, Adafruit_MAX1.SCL, Bauteil1.SCL, R2.Pin_0, Sensor_Stecker1.SCL, Bauteil2.SCL
  GND: MCU1.pin_6, MCU1.pin_14, MCU1.pin_20, MCU1.pin_30, MCU1.pin_34, MCU1.pin_39, Adafruit_MAX1.GND, BAT1.-, Bauteil1.GND, Mod2.GND, S1.Pin_1, S1.Pin_2, Sensor_Stecker1.GND, Bauteil2.GND, J3.GND, Q2.E, R10.Pin_0
  N4: MCU1.pin_7, Sensor_Stecker1.one-wire, R3.Pin_0
  N5: MCU1.pin_8, Mod2.RXD
  N6: MCU1.pin_10, Mod2.TXD
  N7: MCU1.pin_11, D1.anode
  N8: MCU1.pin_16, Mod2.M1
  N9: MCU1.pin_18, Mod2.M0
  N10: MCU1.pin_22, Mod2.AUX
  N11: MCU1.pin_24, J4.pin3
  N12: MCU1.pin_32, R5.Pin_1
  N13: MCU1.pin_36, R4.Pin_1
  N14: MCU1.pin_37, S1.Pin_3, S1.Pin_4
  N15: BAT1.+, Bauteil1.VBAT
  N16: LED1.blue_anode, R4.Pin_0
  N17: LED1.green_anode, R5.Pin_0
  N18: Q1.gate, R6.Pin_0, Q2.C
  N19: Q1.source, R6.Pin_1, J3.5V, S2.Pin_1, S2.Pin_2, J5.pin3
  N20: Q2.B, R8.Pin_1, R9.Pin_1
  N21: R8.Pin_0, D1.cathode
  N22: R9.Pin_0, S2.Pin_3, S2.Pin_4, J5.pin1
  N23: J4.pin1, R10.Pin_1

custom parts:
  Adafruit MAX17048 LiPoly / LiIon Fuel Gauge and Battery Monitor: Low cost Lithium Polymer batteries have revolutionized electronics - they're thin, they're light, they can be regulated down to 3.3V and they're easy to charge. On your phone, there's a little image of a battery cell that tells you the percentage of charge - so you know when you absolutely need to plug it in and when you can stay untethered. The Adafruit MAX17048 LiPoly / LiIon Fuel Gauge and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
  DS3231: The DS3231 RTC.
  ossoyoo-lora-module: Osoyoo Long Distance wireless transceiver Uart LoRa Module.
  Generic female header - 6 pins: Generic female header
  Generic female header - 2 pins: Generic female header
